# Fritzing sketch home automate outside 3 (saved by Fritzing 0.9.3b)

parts:
  M1 = fc-51 [package=THT]
  IC1 = MICROCONTROLLER [package=dil28-3-simon]
  J1 = female pin header, 4 pins [form="♀ (female)"]
  J2 = Camdenboss CTB0158-2 [part_number=CTB0158-2 package=THT]
  J3 = male pin header, 3 pins [form="♂ (male)"]
  J4 = male pin header, 3 pins [form="♂ (male)"]
  J5 = male pin header, 3 pins [form="♂ (male)"]
  J6 = female pin header, 2 pins [form="♀ (female)"]
  J7 = male pin header, 3 pins [form="♂ (male)"]
  J8 = male pin header, 3 pins [form="♂ (male)"]
  LED1 = LED - 3mm [color="Red (633nm)" package="3 mm [THT]"]
  C1 = Capacitor [package=cap-pth-small2]
  C2 = Capacitor [package=cap-pth-small2]
  XTAL1 = Crystal [frequency="16 Mhz" package=THT]
  R1 = Resistor [tolerance=±5% resistance=15k package="0402 [SMD]"]
  R2 = Resistor [tolerance=±5% resistance=15k package="0402 [SMD]"]
  S1 = Momentary Switch [package=ksa_sealed_tac_switch]
  PIR1 = PIR sensor
  PIR2 = PIR sensor
  R3 = Rotary Potentiometer (Large) [maximum_resistance=100kΩ package=THT]
  KY-1 = Keyes Relay [package=THT]
  R4 = Photocell (LDR) [package=THT]

nets:
  N1: M1.pin1, IC1.PD2(INT0), J7.pin1
  N2: M1.pin2, J1.pin3, J2.pin1, J5.pin1, J7.pin3, J8.pin3, LED1.cathode, C1.1, R1.Pin_1, S1.4, R3.leg2, KY-1.ground
  VDD: M1.pin3, IC1.PC6(_RESET), J1.pin4, J3.pin2, J4.pin2, J7.pin2, J8.pin2, S1.2, PIR1.VDD, PIR2.VDD, KY-1.power
  N3: IC1.PD0(RXD), J1.pin1
  N4: IC1.PD1(TXD), J1.pin2
  N5: IC1.PD3(INT1), J8.pin1, KY-1.signal
  N6: IC1.PB6(XTAL1_TOSC1), C1.2, XTAL1.pin_1
  N7: IC1.PB7(XTAL2_TOSC2), C2.1, XTAL1.pin_0
  N8: IC1.PD5(T1), J3.pin1, PIR2.SIG
  N9: IC1.PD6(AIN0), J4.pin1, PIR1.SIG
  N10: IC1.PB5(SCK), LED1.anode
  N11: IC1.PC0(ADC0), R4.pin_0
  N12: IC1.PC5(ADC5_SCL), J5.pin3, R3.leg1
  N13: J2.pin2, J5.pin2, J6.pin1, R2.Pin_0, R3.wiper, R4.pin_1
  GND: J3.pin3, J4.pin3, C2.2, PIR1.GND, PIR2.GND

notes:
  Orange wire is for i/p
  Green wire is for o/p
  pink is RX of atmega8
  purple is TX of atmega8

custom parts:
  Keyes Relay: The Keyes 5V relay module is suitable for SCM development, home appliance control. It uses a 5V~12V TIL control signal which can control DC / AC signal.
